// Logisim project project.circ as structural Verilog
module MUX_2 (
  input  in_1,
  input  in_2,
  input  in_3,
  output out_4
);

  wire and_1_out, and_2_out, not_1_out;

  not not_1 (not_1_out, in_3);
  and and_1 (and_1_out, in_1, in_3);
  and and_2 (and_2_out, in_2, not_1_out);
  or or_1 (out_4, and_1_out, and_2_out);
endmodule

module MUX_2_3 (
  input  in_1,
  input  in_2,
  input  in_3,
  output out_4
);

  wire not_1_out;

  not not_1 (not_1_out, in_3);
  assign out_4 = in_3 ? in_1 : 1'bz;  // Controlled_Buffer controlled_buffer_1
  assign out_4 = not_1_out ? in_2 : 1'bz;  // Controlled_Buffer controlled_buffer_2
endmodule

module MUX_4 (
  input  in_1,
  input  in_2,
  input  in_3,
  input  in_4,
  input  in_5,
  input  in_6,
  output out_7
);

  wire multiplexer_1_out, multiplexer_2_out;

  Multiplexer multiplexer_1 (.in0(in_1), .in1(in_2), .out(multiplexer_1_out), .sel(in_5));
  Multiplexer multiplexer_2 (.in0(in_3), .in1(in_4), .out(multiplexer_2_out), .sel(in_5));
  Multiplexer multiplexer_3 (.in0(multiplexer_1_out), .in1(multiplexer_2_out), .out(out_7), .sel(in_6));
endmodule

module Encoder_83 (
  input  in_1,
  input  in_2,
  input  in_3,
  input  in_4,
  input  in_5,
  input  in_6,
  input  in_7,
  input  in_8,
  output out_9,
  output out_10,
  output out_11
);

  or or_1 (out_9, in_8, in_7, in_6, in_5);
  or or_2 (out_10, in_8, in_7, in_4, in_3);
  or or_3 (out_11, in_8, in_6, in_4, in_2);
endmodule

module PreEncoder_83 (
  input  in_1,
  input  in_2,
  input  in_3,
  input  in_4,
  input  in_5,
  input  in_6,
  input  in_7,
  input  in_8,
  output out_9,
  output out_10,
  output out_11
);

  wire and_1_out, and_2_out, and_3_out, and_4_out, and_5_out, and_6_out, and_7_out, nor_1_out, nor_2_out,
       not_1_out, not_2_out, not_3_out, not_4_out, not_5_out;

  and and_1 (and_1_out, not_1_out, in_7);
  not not_1 (not_1_out, in_8);
  not not_2 (not_2_out, and_1_out);
  and and_2 (and_2_out, not_2_out, not_1_out, in_6);
  not not_3 (not_3_out, and_2_out);
  and and_3 (and_3_out, not_3_out, not_2_out, not_1_out, in_5);
  nor nor_1 (nor_1_out, in_8, and_1_out, and_2_out, and_3_out);
  and and_4 (and_4_out, nor_1_out, in_4);
  not not_4 (not_4_out, and_4_out);
  and and_5 (and_5_out, not_4_out, nor_1_out, in_3);
  not not_5 (not_5_out, and_5_out);
  and and_6 (and_6_out, nor_2_out, nor_1_out, in_1);
  and and_7 (and_7_out, not_5_out, not_4_out, nor_1_out, in_2);
  nor nor_2 (nor_2_out, nor_1_out, and_4_out, and_5_out, and_7_out);
  or or_1 (out_9, and_7_out, and_4_out, and_2_out, in_8);
  or or_2 (out_10, and_5_out, and_4_out, and_1_out, in_8);
  or or_3 (out_11, and_3_out, and_2_out, and_1_out, in_8);
endmodule

module Decoder_38 (
  input  in_1,
  input  in_2,
  input  in_3,
  output out_4,
  output out_5,
  output out_6,
  output out_7,
  output out_8,
  output out_9,
  output out_10,
  output out_11
);

  wire not_1_out, not_2_out, not_3_out;

  not not_1 (not_1_out, in_1);
  not not_2 (not_2_out, in_2);
  not not_3 (not_3_out, in_3);
  and and_1 (out_4, not_1_out, not_2_out, not_3_out);
  and and_2 (out_5, in_1, not_2_out, not_3_out);
  and and_3 (out_6, not_1_out, in_2, not_3_out);
  and and_4 (out_7, in_1, in_2, not_3_out);
  and and_5 (out_8, not_1_out, not_2_out, in_3);
  and and_6 (out_9, in_1, not_2_out, in_3);
  and and_7 (out_10, not_1_out, in_2, in_3);
  and and_8 (out_11, in_1, in_2, in_3);
endmodule

module SR_Latch (
  input  S,
  input  R,
  output out_3,
  output Q
);

  wire or_1_out, or_2_out;

  or or_1 (or_1_out, S, Q);
  or or_2 (or_2_out, out_3, R);
  not not_1 (out_3, or_1_out);
  not not_2 (Q, or_2_out);
endmodule

module D_Latch (
  input  CLK,
  input  D,
  output out_3,
  output Q
);

  wire and_1_out, and_2_out, not_1_out;

  not not_1 (not_1_out, D);
  and and_1 (and_1_out, CLK, D);
  and and_2 (and_2_out, CLK, not_1_out);
  SR_Latch sr_latch_1 (.S(and_1_out), .R(and_2_out), .out_3(out_3), .Q(Q));
endmodule

module D_Trigger (
  input  CLK,
  input  RST,
  input  D,
  input  EN,
  output out_5,
  output Q
);

  wire and_1_out, and_2_out, d_latch_1_q, multiplexer_1_out, not_1_out, not_2_out, or_1_out, or_2_out;

  not not_1 (not_1_out, RST);
  Multiplexer multiplexer_1 (.in0(Q), .in1(D), .out(multiplexer_1_out), .sel(EN));
  or or_1 (or_1_out, RST, not_2_out);
  not not_2 (not_2_out, CLK);
  and and_1 (and_1_out, multiplexer_1_out, not_1_out);
  or or_2 (or_2_out, RST, CLK);
  and and_2 (and_2_out, d_latch_1_q, not_1_out);
  D_Latch d_latch_1 (.CLK(or_1_out), .D(and_1_out), .Q(d_latch_1_q));  // open: out_3
  D_Latch d_latch_2 (.CLK(or_2_out), .D(and_2_out), .out_3(out_5), .Q(Q));
endmodule

module Register_4 (
  input  [3:0] D_in,
  input  EN,
  input  RST,
  input  CLK,
  output [3:0] D_out
);

  D_Trigger d_trigger_1 (.CLK(CLK), .RST(RST), .D(D_in[0]), .EN(EN), .Q(D_out[0]));  // open: out_5
  D_Trigger d_trigger_2 (.CLK(CLK), .RST(RST), .D(D_in[1]), .EN(EN), .Q(D_out[1]));  // open: out_5
  D_Trigger d_trigger_3 (.CLK(CLK), .RST(RST), .D(D_in[2]), .EN(EN), .Q(D_out[2]));  // open: out_5
  D_Trigger d_trigger_4 (.CLK(CLK), .RST(RST), .D(D_in[3]), .EN(EN), .Q(D_out[3]));  // open: out_5
endmodule

module Register_8 (
  input  [1:0] S,
  input  [7:0] D_in,
  input  RST,
  input  CLK,
  input  Algor,
  output [7:0] D_out
);

  wire multiplexer_1_out, multiplexer_2_out, multiplexer_3_out, multiplexer_4_out, multiplexer_5_out,
       multiplexer_6_out, multiplexer_7_out, multiplexer_8_out, multiplexer_9_out;

  Multiplexer multiplexer_1 (.in0(1'b0), .in1(D_out[7]), .out(multiplexer_1_out), .sel(Algor));
  Multiplexer #(.select(2)) multiplexer_2 (
    .in0(D_out[0]), .in1(D_out[1]), .in2(1'b0), .in3(D_in[0]), .out(multiplexer_2_out), .sel(S));
  Multiplexer #(.select(2)) multiplexer_3 (
    .in0(D_out[1]), .in1(D_out[2]), .in2(D_out[0]), .in3(D_in[1]), .out(multiplexer_3_out), .sel(S));
  Multiplexer #(.select(2)) multiplexer_4 (
    .in0(D_out[2]), .in1(D_out[3]), .in2(D_out[1]), .in3(D_in[2]), .out(multiplexer_4_out), .sel(S));
  Multiplexer #(.select(2)) multiplexer_5 (
    .in0(D_out[3]), .in1(D_out[4]), .in2(D_out[2]), .in3(D_in[3]), .out(multiplexer_5_out), .sel(S));
  Multiplexer #(.select(2)) multiplexer_6 (
    .in0(D_out[4]), .in1(D_out[5]), .in2(D_out[3]), .in3(D_in[4]), .out(multiplexer_6_out), .sel(S));
  Multiplexer #(.select(2)) multiplexer_7 (
    .in0(D_out[5]), .in1(D_out[6]), .in2(D_out[4]), .in3(D_in[5]), .out(multiplexer_7_out), .sel(S));
  Multiplexer #(.select(2)) multiplexer_8 (
    .in0(D_out[6]), .in1(D_out[7]), .in2(D_out[5]), .in3(D_in[6]), .out(multiplexer_8_out), .sel(S));
  Multiplexer #(.select(2)) multiplexer_9 (
    .in0(D_out[7]), .in1(multiplexer_1_out), .in2(D_out[6]), .in3(D_in[7]), .out(multiplexer_9_out), .sel(S));
  D_Trigger d_trigger_1 (.CLK(CLK), .RST(RST), .D(multiplexer_2_out), .EN(1'b1), .Q(D_out[0]));  // open: out_5
  D_Trigger d_trigger_2 (.CLK(CLK), .RST(RST), .D(multiplexer_3_out), .EN(1'b1), .Q(D_out[1]));  // open: out_5
  D_Trigger d_trigger_3 (.CLK(CLK), .RST(RST), .D(multiplexer_4_out), .EN(1'b1), .Q(D_out[2]));  // open: out_5
  D_Trigger d_trigger_4 (.CLK(CLK), .RST(RST), .D(multiplexer_5_out), .EN(1'b1), .Q(D_out[3]));  // open: out_5
  D_Trigger d_trigger_5 (.CLK(CLK), .RST(RST), .D(multiplexer_6_out), .EN(1'b1), .Q(D_out[4]));  // open: out_5
  D_Trigger d_trigger_6 (.CLK(CLK), .RST(RST), .D(multiplexer_7_out), .EN(1'b1), .Q(D_out[5]));  // open: out_5
  D_Trigger d_trigger_7 (.CLK(CLK), .RST(RST), .D(multiplexer_8_out), .EN(1'b1), .Q(D_out[6]));  // open: out_5
  D_Trigger d_trigger_8 (.CLK(CLK), .RST(RST), .D(multiplexer_9_out), .EN(1'b1), .Q(D_out[7]));  // open: out_5
endmodule

module Counter_44 (
  input  RST,
  input  CLK,
  output [7:0] CNT
);

  wire comparator_1_eq, or_1_out;
  wire [7:0] adder_1_out;

  or or_1 (or_1_out, RST, comparator_1_eq);
  Adder adder_1 (.a(CNT), .b(8'h1), .out(adder_1_out));  // open: cin, cout
  Register_8 register_8_1 (.S(2'b11), .D_in(adder_1_out), .RST(or_1_out), .CLK(CLK), .Algor(1'b0), .D_out(CNT));
  Comparator comparator_1 (.a(CNT), .b(8'h2c), .eq(comparator_1_eq));  // open: gt, lt
endmodule

module Detech_01 (
  input  CLK,
  input  RST,
  input  A,
  output Y
);

  wire and_1_out, d_trigger_1_q, not_1_out;

  not not_1 (not_1_out, A);
  and and_1 (and_1_out, d_trigger_1_q, A);
  D_Trigger d_trigger_1 (.CLK(CLK), .RST(RST), .D(not_1_out), .EN(1'b1), .Q(d_trigger_1_q));  // open: out_5
  D_Trigger d_trigger_2 (.CLK(CLK), .RST(RST), .D(and_1_out), .EN(1'b1), .Q(Y));  // open: out_5
endmodule

module Half_Adder (
  input  A,
  input  B,
  output S,
  output C
);

  xor xor_1 (S, A, B);
  and and_1 (C, A, B);
endmodule

module Full_Adder (
  input  A,
  input  B,
  input  C_in,
  output C_out,
  output S
);

  wire half_adder_1_c, half_adder_1_s, half_adder_2_c;

  Half_Adder half_adder_1 (.A(A), .B(B), .S(half_adder_1_s), .C(half_adder_1_c));
  Half_Adder half_adder_2 (.A(half_adder_1_s), .B(C_in), .S(S), .C(half_adder_2_c));
  or or_1 (C_out, half_adder_1_c, half_adder_2_c);
endmodule

module RCA (
  input  [31:0] A,
  input  [31:0] B,
  input  C_in,
  output [31:0] S,
  output C_out
);

  wire full_adder_1_c_out, full_adder_2_c_out, full_adder_3_c_out, full_adder_4_c_out, full_adder_5_c_out,
       full_adder_6_c_out, full_adder_7_c_out, full_adder_8_c_out, full_adder_9_c_out, full_adder_10_c_out,
       full_adder_11_c_out, full_adder_12_c_out, full_adder_13_c_out, full_adder_14_c_out,
       full_adder_15_c_out, full_adder_16_c_out, full_adder_17_c_out, full_adder_18_c_out,
       full_adder_19_c_out, full_adder_20_c_out, full_adder_21_c_out, full_adder_22_c_out,
       full_adder_23_c_out, full_adder_24_c_out, full_adder_25_c_out, full_adder_26_c_out,
       full_adder_27_c_out, full_adder_28_c_out, full_adder_29_c_out, full_adder_30_c_out,
       full_adder_31_c_out;

  Full_Adder full_adder_1 (.A(A[0]), .B(B[0]), .C_in(C_in), .C_out(full_adder_1_c_out), .S(S[0]));
  Full_Adder full_adder_2 (.A(A[1]), .B(B[1]), .C_in(full_adder_1_c_out), .C_out(full_adder_2_c_out), .S(S[1]));
  Full_Adder full_adder_3 (.A(A[2]), .B(B[2]), .C_in(full_adder_2_c_out), .C_out(full_adder_3_c_out), .S(S[2]));
  Full_Adder full_adder_4 (.A(A[3]), .B(B[3]), .C_in(full_adder_3_c_out), .C_out(full_adder_4_c_out), .S(S[3]));
  Full_Adder full_adder_5 (.A(A[4]), .B(B[4]), .C_in(full_adder_4_c_out), .C_out(full_adder_5_c_out), .S(S[4]));
  Full_Adder full_adder_6 (.A(A[5]), .B(B[5]), .C_in(full_adder_5_c_out), .C_out(full_adder_6_c_out), .S(S[5]));
  Full_Adder full_adder_7 (.A(A[6]), .B(B[6]), .C_in(full_adder_6_c_out), .C_out(full_adder_7_c_out), .S(S[6]));
  Full_Adder full_adder_8 (.A(A[7]), .B(B[7]), .C_in(full_adder_7_c_out), .C_out(full_adder_8_c_out), .S(S[7]));
  Full_Adder full_adder_9 (.A(A[8]), .B(B[8]), .C_in(full_adder_8_c_out), .C_out(full_adder_9_c_out), .S(S[8]));
  Full_Adder full_adder_10 (.A(A[9]), .B(B[9]), .C_in(full_adder_9_c_out), .C_out(full_adder_10_c_out), .S(S[9]));
  Full_Adder full_adder_11 (.A(A[10]), .B(B[10]), .C_in(full_adder_10_c_out), .C_out(full_adder_11_c_out), .S(S[10]));
  Full_Adder full_adder_12 (.A(A[11]), .B(B[11]), .C_in(full_adder_11_c_out), .C_out(full_adder_12_c_out), .S(S[11]));
  Full_Adder full_adder_13 (.A(A[12]), .B(B[12]), .C_in(full_adder_12_c_out), .C_out(full_adder_13_c_out), .S(S[12]));
  Full_Adder full_adder_14 (.A(A[13]), .B(B[13]), .C_in(full_adder_13_c_out), .C_out(full_adder_14_c_out), .S(S[13]));
  Full_Adder full_adder_15 (.A(A[14]), .B(B[14]), .C_in(full_adder_14_c_out), .C_out(full_adder_15_c_out), .S(S[14]));
  Full_Adder full_adder_16 (.A(A[15]), .B(B[15]), .C_in(full_adder_15_c_out), .C_out(full_adder_16_c_out), .S(S[15]));
  Full_Adder full_adder_17 (.A(A[16]), .B(B[16]), .C_in(full_adder_16_c_out), .C_out(full_adder_17_c_out), .S(S[16]));
  Full_Adder full_adder_18 (.A(A[17]), .B(B[17]), .C_in(full_adder_17_c_out), .C_out(full_adder_18_c_out), .S(S[17]));
  Full_Adder full_adder_19 (.A(A[18]), .B(B[18]), .C_in(full_adder_18_c_out), .C_out(full_adder_19_c_out), .S(S[18]));
  Full_Adder full_adder_20 (.A(A[19]), .B(B[19]), .C_in(full_adder_19_c_out), .C_out(full_adder_20_c_out), .S(S[19]));
  Full_Adder full_adder_21 (.A(A[20]), .B(B[20]), .C_in(full_adder_20_c_out), .C_out(full_adder_21_c_out), .S(S[20]));
  Full_Adder full_adder_22 (.A(A[21]), .B(B[21]), .C_in(full_adder_21_c_out), .C_out(full_adder_22_c_out), .S(S[21]));
  Full_Adder full_adder_23 (.A(A[22]), .B(B[22]), .C_in(full_adder_22_c_out), .C_out(full_adder_23_c_out), .S(S[22]));
  Full_Adder full_adder_24 (.A(A[23]), .B(B[23]), .C_in(full_adder_23_c_out), .C_out(full_adder_24_c_out), .S(S[23]));
  Full_Adder full_adder_25 (.A(A[24]), .B(B[24]), .C_in(full_adder_24_c_out), .C_out(full_adder_25_c_out), .S(S[24]));
  Full_Adder full_adder_26 (.A(A[25]), .B(B[25]), .C_in(full_adder_25_c_out), .C_out(full_adder_26_c_out), .S(S[25]));
  Full_Adder full_adder_27 (.A(A[26]), .B(B[26]), .C_in(full_adder_26_c_out), .C_out(full_adder_27_c_out), .S(S[26]));
  Full_Adder full_adder_28 (.A(A[27]), .B(B[27]), .C_in(full_adder_27_c_out), .C_out(full_adder_28_c_out), .S(S[27]));
  Full_Adder full_adder_29 (.A(A[28]), .B(B[28]), .C_in(full_adder_28_c_out), .C_out(full_adder_29_c_out), .S(S[28]));
  Full_Adder full_adder_30 (.A(A[29]), .B(B[29]), .C_in(full_adder_29_c_out), .C_out(full_adder_30_c_out), .S(S[29]));
  Full_Adder full_adder_31 (.A(A[30]), .B(B[30]), .C_in(full_adder_30_c_out), .C_out(full_adder_31_c_out), .S(S[30]));
  Full_Adder full_adder_32 (.A(A[31]), .B(B[31]), .C_in(full_adder_31_c_out), .C_out(C_out), .S(S[31]));
endmodule

module CLA_8 (
  input  C_in,
  input  [7:0] A,
  input  [7:0] B,
  output [7:0] S,
  output C_out
);

  wire and_1_out, and_2_out, and_3_out, and_4_out, and_5_out, and_6_out, and_7_out, and_8_out, and_9_out,
       and_10_out, and_11_out, and_12_out, and_13_out, and_14_out, and_15_out, and_16_out, and_17_out,
       and_18_out, and_19_out, and_20_out, and_21_out, and_22_out, and_23_out, and_24_out, and_25_out,
       and_26_out, and_27_out, and_28_out, and_29_out, and_30_out, and_31_out, and_32_out, and_33_out,
       and_34_out, and_35_out, and_36_out, or_1_out, or_2_out, or_3_out, or_4_out, or_5_out, or_6_out,
       or_7_out;
  wire [7:0] G0_out, P0_out;

  and G0 (G0_out[0], A[0], B[0]);
  or P0 (P0_out[0], A[0], B[0]);
  and G1 (G0_out[1], A[1], B[1]);
  or P1 (P0_out[1], A[1], B[1]);
  and G2 (G0_out[2], A[2], B[2]);
  or P2 (P0_out[2], A[2], B[2]);
  and G3 (G0_out[3], A[3], B[3]);
  or P3 (P0_out[3], A[3], B[3]);
  and G4 (G0_out[4], A[4], B[4]);
  or P4 (P0_out[4], A[4], B[4]);
  and G5 (G0_out[5], A[5], B[5]);
  or P5 (P0_out[5], A[5], B[5]);
  and G6 (G0_out[6], A[6], B[6]);
  or P6 (P0_out[6], A[6], B[6]);
  and G7 (G0_out[7], A[7], B[7]);
  or P7 (P0_out[7], A[7], B[7]);
  and and_1 (and_1_out, P0_out[0], C_in);
  or or_1 (or_1_out, and_1_out, G0_out[0]);
  and and_2 (and_2_out, P0_out[0], P0_out[1], C_in);
  and and_3 (and_3_out, P0_out[1], G0_out[0]);
  or or_2 (or_2_out, and_2_out, and_3_out, G0_out[1]);
  and and_4 (and_4_out, P0_out[0], P0_out[1], P0_out[2], C_in);
  and and_5 (and_5_out, P0_out[1], P0_out[2], G0_out[0]);
  or or_3 (or_3_out, and_4_out, and_5_out, and_6_out, G0_out[2]);
  and and_6 (and_6_out, P0_out[2], G0_out[1]);
  and and_7 (and_7_out, P0_out[0], P0_out[1], P0_out[2], P0_out[3], C_in);
  and and_8 (and_8_out, P0_out[1], P0_out[2], P0_out[3], G0_out[0]);
  and and_9 (and_9_out, P0_out[2], P0_out[3], G0_out[1]);
  and and_10 (and_10_out, P0_out[3], G0_out[2]);
  and and_11 (and_11_out, P0_out[0], P0_out[1], P0_out[2], P0_out[3], P0_out[4], C_in);
  and and_12 (and_12_out, P0_out[1], P0_out[2], P0_out[3], P0_out[4], G0_out[0]);
  and and_13 (and_13_out, P0_out[2], P0_out[3], P0_out[4], G0_out[1]);
  and and_14 (and_14_out, P0_out[3], P0_out[4], G0_out[2]);
  and and_15 (and_15_out, P0_out[4], G0_out[3]);
  and and_16 (and_16_out, P0_out[0], P0_out[1], P0_out[2], P0_out[3], P0_out[4], P0_out[5], C_in);
  and and_17 (and_17_out, P0_out[1], P0_out[2], P0_out[3], P0_out[4], P0_out[5], G0_out[0]);
  and and_18 (and_18_out, P0_out[2], P0_out[3], P0_out[4], P0_out[5], G0_out[1]);
  and and_19 (and_19_out, P0_out[3], P0_out[4], P0_out[5], G0_out[2]);
  and and_20 (and_20_out, P0_out[4], P0_out[5], G0_out[3]);
  and and_21 (and_21_out, P0_out[5], G0_out[4]);
  and and_22 (and_22_out, P0_out[0], P0_out[1], P0_out[2], P0_out[3], P0_out[4], P0_out[5], P0_out[6], C_in);
  and and_23 (and_23_out, P0_out[1], P0_out[2], P0_out[3], P0_out[4], P0_out[5], P0_out[6], G0_out[0]);
  and and_24 (and_24_out, P0_out[2], P0_out[3], P0_out[4], P0_out[5], P0_out[6], G0_out[1]);
  and and_25 (and_25_out, P0_out[3], P0_out[4], P0_out[5], P0_out[6], G0_out[2]);
  and and_26 (and_26_out, P0_out[4], P0_out[5], P0_out[6], G0_out[3]);
  and and_27 (and_27_out, P0_out[5], P0_out[6], G0_out[4]);
  and and_28 (and_28_out, P0_out[6], G0_out[5]);
  and and_29 (and_29_out, P0_out[0], P0_out[1], P0_out[2], P0_out[3], P0_out[4], P0_out[5], P0_out[6], P0_out[7], C_in);
  and and_30 (and_30_out, P0_out[1], P0_out[2], P0_out[3], P0_out[4], P0_out[5], P0_out[6], P0_out[7], G0_out[0]);
  and and_31 (and_31_out, P0_out[2], P0_out[3], P0_out[4], P0_out[5], P0_out[6], P0_out[7], G0_out[1]);
  and and_32 (and_32_out, P0_out[3], P0_out[4], P0_out[5], P0_out[6], P0_out[7], G0_out[2]);
  and and_33 (and_33_out, P0_out[4], P0_out[5], P0_out[6], P0_out[7], G0_out[3]);
  and and_34 (and_34_out, P0_out[5], P0_out[6], P0_out[7], G0_out[4]);
  and and_35 (and_35_out, P0_out[6], P0_out[7], G0_out[5]);
  and and_36 (and_36_out, P0_out[7], G0_out[6]);
  or or_4 (or_4_out, and_7_out, and_8_out, and_9_out, and_10_out, G0_out[3]);
  or or_5 (or_5_out, and_11_out, and_12_out, and_13_out, and_14_out, and_15_out, G0_out[4]);
  or or_6 (or_6_out, and_16_out, and_17_out, and_18_out, and_19_out, and_20_out, and_21_out, G0_out[5]);
  or or_7 (or_7_out, and_22_out, and_23_out, and_24_out, and_25_out, and_26_out, and_27_out, and_28_out, G0_out[6]);
  or or_8 (C_out, and_29_out, and_30_out, and_31_out, and_32_out, and_33_out, and_34_out, and_35_out, and_36_out, G0_out[7]);
  Full_Adder full_adder_1 (.A(A[0]), .B(B[0]), .C_in(C_in), .S(S[0]));  // open: C_out
  Full_Adder full_adder_2 (.A(A[1]), .B(B[1]), .C_in(or_1_out), .S(S[1]));  // open: C_out
  Full_Adder full_adder_3 (.A(A[2]), .B(B[2]), .C_in(or_2_out), .S(S[2]));  // open: C_out
  Full_Adder full_adder_4 (.A(A[3]), .B(B[3]), .C_in(or_3_out), .S(S[3]));  // open: C_out
  Full_Adder full_adder_5 (.A(A[4]), .B(B[4]), .C_in(or_4_out), .S(S[4]));  // open: C_out
  Full_Adder full_adder_6 (.A(A[5]), .B(B[5]), .C_in(or_5_out), .S(S[5]));  // open: C_out
  Full_Adder full_adder_7 (.A(A[6]), .B(B[6]), .C_in(or_6_out), .S(S[6]));  // open: C_out
  Full_Adder full_adder_8 (.A(A[7]), .B(B[7]), .C_in(or_7_out), .S(S[7]));  // open: C_out
endmodule

module CLA_32 (
  input  [31:0] A,
  input  [31:0] B,
  input  C_in,
  output [31:0] S,
  output C_out
);

  wire cla_8_1_c_out, cla_8_2_c_out, cla_8_3_c_out;

  CLA_8 cla_8_1 (.C_in(C_in), .A(A[7:0]), .B(B[7:0]), .S(S[7:0]), .C_out(cla_8_1_c_out));
  CLA_8 cla_8_2 (.C_in(cla_8_1_c_out), .A(A[15:8]), .B(B[15:8]), .S(S[15:8]), .C_out(cla_8_2_c_out));
  CLA_8 cla_8_3 (.C_in(cla_8_2_c_out), .A(A[23:16]), .B(B[23:16]), .S(S[23:16]), .C_out(cla_8_3_c_out));
  CLA_8 cla_8_4 (.C_in(cla_8_3_c_out), .A(A[31:24]), .B(B[31:24]), .S(S[31:24]), .C_out(C_out));
endmodule

module ALU (
  input  [31:0] A,
  input  [31:0] B,
  input  [3:0] OP,
  output [31:0] S,
  output SF,
  output OF1,
  output ZF,
  output CF1,
  output PF
);

  wire cla_32_1_c_out, cla_32_2_c_out;
  wire [0:0] comparator_1_lt;
  wire [31:0] and_1_out, cla_32_1_s, cla_32_2_s, nor_1_out, not_1_out, or_1_out, shifter_1_out, xor_1_out;

  assign not_1_out = ~B;  // NOT_Gate not_1, 32 bits wide
  assign and_1_out = A & B;  // AND_Gate and_1, 32 bits wide
  assign or_1_out = A | B;  // OR_Gate or_1, 32 bits wide
  assign xor_1_out = A ^ B;  // XOR_Gate xor_1, 32 bits wide
  assign nor_1_out = ~(A | B);  // NOR_Gate nor_1, 32 bits wide
  Comparator #(.width(32)) comparator_1 (.a(A), .b(B), .lt(comparator_1_lt[0]));  // open: gt, eq
  Shifter #(.width(32)) shifter_1 (.in(A), .\dist (B[4:0]), .out(shifter_1_out));
  CLA_32 cla_32_1 (.A(A), .B(B), .C_in(1'b0), .S(cla_32_1_s), .C_out(cla_32_1_c_out));
  CLA_32 cla_32_2 (.A(A), .B(not_1_out), .C_in(1'b1), .S(cla_32_2_s), .C_out(cla_32_2_c_out));
  Multiplexer #(.select(4)) multiplexer_1 (
    .in0(1'b0), .in1(1'b0), .in2(1'b0), .in3(1'b0), .in4(cla_32_1_c_out), .in5(cla_32_2_c_out), .in6(1'b0),
    .in7(1'b0), .in8(1'b0), .in9(1'b0), .in10(1'b0), .in11(1'b0), .in12(1'b0), .in13(1'b0), .in14(1'b0),
    .in15(1'b0), .out(CF1), .sel(OP));
  Multiplexer #(.select(4), .width(32)) multiplexer_2 (
    .in0(and_1_out), .in1(or_1_out), .in2(xor_1_out), .in3(nor_1_out), .in4(cla_32_1_s), .in5(cla_32_2_s),
    .in6({{31{1'b0}}, comparator_1_lt[0]}), .in7(shifter_1_out), .out(S), .sel(OP));  // open: in8, in9, in10, in11, in12, in13, in14, in15
  xor xor_2 (OF1, A[31], S[31], B[31], CF1);
  Comparator #(.width(32)) comparator_2 (.a(S), .b({32{1'b0}}), .eq(ZF));  // open: gt, lt
  xor xor_3 (PF, S[0], S[1], S[2], S[3], S[4], S[5], S[6], S[7], S[8], S[9], S[10], S[11], S[12], S[13], S[14], S[15], S[16], S[17], S[18], S[19], S[20], S[21], S[22], S[23], S[24], S[25], S[26], S[27], S[28], S[29], S[30], S[31], 1'b0);

  assign SF = S[31];
endmodule
